# Fritzing sketch P1 Fritzing Example (saved by Fritzing 0.9.2b)
breadboards: 1

parts:
  C7 = Ceramic Capacitor [capacitance=0.10µF package="0805 [SMD, multilayer]"]
  C9 = Ceramic Capacitor [capacitance=10µF package="0805 [SMD, multilayer]"]
  C10 = Ceramic Capacitor [capacitance=0.10µF package="0805 [SMD, multilayer]"]
  C11 = Ceramic Capacitor [capacitance=10µF package="0805 [SMD, multilayer]"]
  C12 = Ceramic Capacitor [capacitance=0.10µF package="0805 [SMD, multilayer]"]
  C13 = Ceramic Capacitor [capacitance=0.10µF package="0805 [SMD, multilayer]"]
  C14 = Ceramic Capacitor [capacitance=10µF package="0805 [SMD, multilayer]"]
  C15 = Ceramic Capacitor [capacitance=10µF package="0805 [SMD, multilayer]"]
  X1 = USB Connectors [package=usb-microb]
  R1 = Resistor [tolerance=±5% resistance=22 package="0805 [SMD]"]
  R2 = Resistor [tolerance=±5% resistance=22 package="0805 [SMD]"]
  S1 = SWITCH-MOMENTARY-2 [package=tactile_switch_smd]
  S2 = SWITCH-MOMENTARY-2 [package=tactile_switch_smd]
  C16 = Ceramic Capacitor [capacitance=0.10µF package="0805 [SMD, multilayer]"]
  R3 = Resistor [tolerance=±5% resistance=10k package="0805 [SMD]"]
  R4 = Resistor [tolerance=±5% resistance=1k package="0805 [SMD]"]
  LED1 = LED - 5mm [color="Red (633nm)" package="5 mm [THT]"]
  R5 = Resistor [tolerance=±5% resistance=1k package="0805 [SMD]"]
  LED2 = LED - 5mm [color="Green (555nm)" package="5 mm [THT]"]
  R6 = Resistor [tolerance=±5% resistance=1k package="0805 [SMD]"]
  R7 = Resistor [tolerance=±5% resistance=1k package="0805 [SMD]"]
  LED3 = LED - 5mm [color="Blue (430nm)" package="5 mm [THT]"]
  LED4 = LED - 5mm [color="Blue (430nm)" package="5 mm [THT]"]
  Part4 = Particle P1 [package=P1]  # not connected

nets:
  3v3: C7.0, C9.0, C10.0, C11.0, C12.0, C13.0, C14.0, C15.0, R3.Pin_0, LED1.anode, LED2.anode, LED3.anode
  GND: C7.1, C9.1, C10.1, C11.1, C12.1, C13.1, C14.1, C15.1, X1.GND, S1.2, S2.2, C16.0, R7.Pin_0
  N1: X1.D+, R1.Pin_0
  N2: X1.D-, R2.Pin_0
  UVCC: X1.VBUS
  USB D+: R1.Pin_1
  USB D-: R2.Pin_1
  SETUP: S1.1
  RESET: S2.1, C16.1, R3.Pin_1
  RGB Red: R4.Pin_0
  N3: R4.Pin_1, LED1.cathode
  RGB Green: R5.Pin_0
  N4: R5.Pin_1, LED2.cathode
  RGB Blue: R6.Pin_0
  N5: R6.Pin_1, LED3.cathode
  N6: R7.Pin_1, LED4.cathode
  D7: LED4.anode
